// Logisim project Oblig1.circ as structural Verilog: 1 circuit, main circuit main
module main (
  input  in_1,
  input  A3,
  input  in_3,
  input  A1,
  input  A0,
  output _256,
  output _128,
  output _64,
  output _32,
  output _16,
  output _8,
  output _4,
  output _2,
  output _1
);

  wire and_1_out, and_2_out, and_3_out, and_4_out, and_5_out, and_6_out, and_7_out, and_8_out, and_9_out,
       and_10_out, and_11_out, and_12_out, or_1_out, xor_2_out, xor_4_out, xor_6_out, xor_7_out, xor_8_out,
       xor_10_out, xor_11_out, xor_13_out, xor_14_out, xor_15_out, xor_17_out, xor_19_out;

  xor xor_1 (_256, and_1_out, in_1);
  xor xor_2 (xor_2_out, in_1, and_2_out);
  and and_1 (and_1_out, xor_2_out, and_3_out);
  xor xor_3 (_128, xor_2_out, and_3_out);
  and and_2 (and_2_out, A3, and_4_out);
  xor xor_4 (xor_4_out, in_1, xor_6_out);
  and and_3 (and_3_out, xor_4_out, and_5_out);
  xor xor_5 (_64, xor_4_out, and_5_out);
  xor xor_6 (xor_6_out, A3, and_4_out);
  and and_4 (and_4_out, in_3, or_1_out);
  and and_5 (and_5_out, xor_8_out, and_8_out);
  or or_1 (or_1_out, and_6_out, and_7_out);
  xor xor_7 (xor_7_out, in_3, or_1_out);
  xor xor_8 (xor_8_out, in_1, xor_7_out);
  xor xor_9 (_32, xor_8_out, and_8_out);
  and and_6 (and_6_out, A1, A3);
  xor xor_10 (xor_10_out, A1, A3);
  and and_7 (and_7_out, xor_10_out, and_10_out);
  xor xor_11 (xor_11_out, xor_13_out, in_1);
  and and_8 (and_8_out, xor_11_out, and_9_out);
  xor xor_12 (_16, xor_11_out, and_9_out);
  xor xor_13 (xor_13_out, xor_10_out, and_10_out);
  and and_9 (and_9_out, xor_15_out, and_11_out);
  and and_10 (and_10_out, in_3, A0);
  xor xor_14 (xor_14_out, A0, in_3);
  xor xor_15 (xor_15_out, in_1, xor_14_out);
  xor xor_16 (_8, xor_15_out, and_11_out);
  xor xor_17 (xor_17_out, in_1, A1);
  and and_11 (and_11_out, xor_17_out, and_12_out);
  and and_12 (and_12_out, xor_19_out, in_1);
  xor xor_18 (_4, xor_17_out, and_12_out);
  xor xor_19 (xor_19_out, in_1, A0);
  xor xor_20 (_2, xor_19_out, in_1);

  assign _1 = 1'b0;

  // Notes on the sheet:
  //   bit fliping
  //   signed/unsigned
  //   full addr
  //   half addr
  //   A2
  //   alltid 0
endmodule
