// Logisim project healthy.circ as structural Verilog: 6 circuits, main circuit main
module main (
  output [3:0] out_1,
  output [7:0] out_2,
  output [7:0] out_3
);

  wire button_1_out, button_2_out, dekoder_1_aaaa, dekoder_1_aaaa_2, dekoder_1_dddd, dekoder_1_dddd_2,
       or_2_out;
  wire [3:0] counter_out_3, rom_1_data;
  wire [7:0] ram_1_data;

  Button button_1 (.out(button_1_out));
  Button button_2 (.out(button_2_out));
  counter counter (.in_1(button_1_out), .out_3(counter_out_3), .in_2(button_2_out));
  Hex_Digit_Display hex_digit_display_1 (.value(counter_out_3));  // open: dp
  dekoder dekoder_1 (
    .signal_in(rom_1_data), .in_2(button_1_out), .dddd(dekoder_1_dddd), .dddd_2(dekoder_1_dddd_2),
    .aaaa(dekoder_1_aaaa), .aaaa_2(dekoder_1_aaaa_2));
  // OR_Gate or_1 has open pins: in1=dekoder_1_aaaa, in2=dekoder_1_aaaa_2, out=open
  ROM #(.addrWidth(4)) rom_1 (.addr(counter_out_3), .data({rom_1_data, out_1}));  // open: sel
  or or_2 (or_2_out, dekoder_1_dddd, dekoder_1_dddd_2, button_2_out);
  Register #(.trigger("falling")) register_1 (.D(out_3), .Q(out_2), .clk(or_2_out), .clr(button_2_out));  // open: en
  _2x4_tristate u_2x4_tristate_1 (.in(out_1), .in_3(out_2), .in_1(dekoder_1_dddd_2), .out_4(out_3));
  RAM #(.addrWidth(4), .bus("separate")) ram_1 (
    .addr(out_1), .din(out_2), .data(ram_1_data), .clk(or_2_out), .clr(button_2_out));  // open: str, sel, ld

  // Notes on the sheet:
  //   count
  //   clear
  //   clock
  //   instruks rom
  //   controller unit
  //   contents of rom_1 (hex, n*v repeats v):
  //   85 97 b1 81 94 a1
  //   instrukser
  //   data forgrener
  //   data ut
  //   data inn
  //   R: register
  //   data ut
endmodule

module counter (
  input  in_1,
  input  in_2,
  output [3:0] out_3
);

  wire adder_1_cout, and_1_out, not_1_out;
  wire [3:0] adder_1_out;

  Register #(.width(4)) register_1 (.D(adder_1_out), .Q(out_3), .clk(and_1_out), .clr(in_2));  // open: en
  and and_1 (and_1_out, in_1, not_1_out);
  not not_1 (not_1_out, adder_1_cout);
  Adder #(.width(4)) adder_1 (.a(out_3), .b(4'b0001), .out(adder_1_out), .cout(adder_1_cout));  // open: cin
endmodule

module _2x4_tristate (
  input  in_1,
  input  [3:0] in,
  input  [7:0] in_3,
  output [7:0] out_4
);

  wire not_1_out;

  assign out_4 = in_1 ? {in_3[7:4], in} : 8'bz;  // Controlled_Buffer controlled_buffer_1
  assign out_4 = not_1_out ? {in, in_3[3:0]} : 8'bz;  // Controlled_Buffer controlled_buffer_2
  not not_1 (not_1_out, in_1);

  // Notes on the sheet:
  //   register input
  //   out
endmodule

module ram (
  input  [3:0] skriv,
  input  [3:0] in_2,
  input  in_3,
  output [3:0] les
);

  wire not_1_out;
  wire [3:0] ram_1_data;

  RAM #(.addrWidth(4), .dataWidth(4), .bus("asynch")) ram_1 (
    .addr(in_2), .data(ram_1_data), .sel(1'b1), .ld(in_3));  // open: clr
  assign ram_1_data = not_1_out ? skriv : 4'bz;  // Controlled_Buffer controlled_buffer_1
  not not_1 (not_1_out, in_3);
  assign les = in_3 ? ram_1_data : 4'bz;  // Controlled_Buffer controlled_buffer_2

  // Notes on the sheet:
  //   posisjon i minne
  //   operasjon skriv/les
endmodule

module instrukser (
  input  [3:0] in_1,
  input  in_2,
  output [7:0] out_3
);

  ROM #(.addrWidth(4)) rom_1 (.addr(in_1), .data(out_3), .sel(in_2));
endmodule

module dekoder (
  input  [3:0] signal_in,
  input  in_2,
  output dddd,
  output dddd_2,
  output aaaa,
  output aaaa_2
);

  wire not_1_out, not_2_out, not_3_out, not_4_out, not_5_out;
  wire [3:0] controlled_buffer_1_out;

  assign controlled_buffer_1_out = in_2 ? signal_in : 4'bz;  // Controlled_Buffer controlled_buffer_1
  assign controlled_buffer_1_out = not_1_out ? 4'b0000 : 4'bz;  // Controlled_Buffer controlled_buffer_2
  not not_1 (not_1_out, in_2);
  not not_2 (not_2_out, controlled_buffer_1_out[2]);
  not not_3 (not_3_out, controlled_buffer_1_out[1]);
  and and_1 (dddd, not_2_out, not_3_out, controlled_buffer_1_out[3], not_4_out);
  not not_4 (not_4_out, controlled_buffer_1_out[0]);
  and and_2 (dddd_2, not_2_out, controlled_buffer_1_out[0], not_3_out, controlled_buffer_1_out[3]);
  and and_3 (aaaa, controlled_buffer_1_out[1], not_2_out, controlled_buffer_1_out[3], not_5_out);
  not not_5 (not_5_out, controlled_buffer_1_out[0]);
  and and_4 (aaaa_2, not_2_out, controlled_buffer_1_out[0], controlled_buffer_1_out[3], controlled_buffer_1_out[1]);
endmodule
