// Logisim project innlevering-01-krets.circ as structural Verilog: 3 circuits, main circuit main
module main (
  input  Signed_or_not,
  input  [3:0] _4_bit_input_number,
  output SignBit,
  output S7,
  output S6,
  output S5,
  output S4,
  output S3,
  output S2,
  output S1,
  output S0
);

  wire fa_1_c_out, fa_1_s, ha_2_c_out, ha_2_s, ha_3_c_out, ha_4_c_out, ha_4_s, ha_5_c_out, ha_6_c_out,
       ha_7_c_out, ha_7_s, ha_8_c_out, ha_9_c_out, ha_10_c_out, xor_1_out, xor_2_out, xor_3_out, xor_4_out,
       xor_5_out, xor_6_out, xor_7_out;

  xor xor_1 (xor_1_out, ha_2_c_out, Signed_or_not);
  HA ha_1 (.IN_1(xor_1_out), .IN_2(ha_3_c_out), .S(S7));  // open: C_OUT
  HA ha_2 (.IN_1(_4_bit_input_number[3]), .C_OUT(ha_2_c_out), .IN_2(ha_4_c_out), .S(ha_2_s));
  xor xor_2 (xor_2_out, ha_2_s, Signed_or_not);
  HA ha_3 (.IN_1(xor_2_out), .C_OUT(ha_3_c_out), .IN_2(ha_5_c_out), .S(S6));
  HA ha_4 (.IN_1(_4_bit_input_number[2]), .C_OUT(ha_4_c_out), .IN_2(fa_1_c_out), .S(ha_4_s));
  xor xor_3 (xor_3_out, ha_4_s, Signed_or_not);
  HA ha_5 (.IN_1(xor_3_out), .C_OUT(ha_5_c_out), .IN_2(ha_6_c_out), .S(S5));
  FA fa_1 (
    .C_OUT(fa_1_c_out), .IN_1(_4_bit_input_number[3]), .S(fa_1_s), .IN_2(_4_bit_input_number[1]),
    .C_IN(ha_7_c_out));
  xor xor_4 (xor_4_out, fa_1_s, Signed_or_not);
  HA ha_6 (.IN_1(xor_4_out), .C_OUT(ha_6_c_out), .IN_2(ha_8_c_out), .S(S4));
  HA ha_7 (.IN_1(_4_bit_input_number[2]), .C_OUT(ha_7_c_out), .IN_2(_4_bit_input_number[0]), .S(ha_7_s));
  xor xor_5 (xor_5_out, ha_7_s, Signed_or_not);
  HA ha_8 (.IN_1(xor_5_out), .C_OUT(ha_8_c_out), .IN_2(ha_9_c_out), .S(S3));
  xor xor_6 (xor_6_out, _4_bit_input_number[1], Signed_or_not);
  HA ha_9 (.IN_1(xor_6_out), .C_OUT(ha_9_c_out), .IN_2(ha_10_c_out), .S(S2));
  Hex_Digit_Display hex_digit_display_1 (.value({S3, S2, S1, 1'b0}));  // open: dp
  Hex_Digit_Display hex_digit_display_2 (.value({S7, S6, S5, S4}));  // open: dp
  xor xor_7 (xor_7_out, _4_bit_input_number[0], Signed_or_not);
  HA ha_10 (.IN_1(xor_7_out), .C_OUT(ha_10_c_out), .IN_2(Signed_or_not), .S(S1));

  assign S0 = 1'b0;
  assign SignBit = Signed_or_not;

  // Notes on the sheet:
  //   P7
  //   Overflow
  //   P6
  //   P5
  //   P4
  //   P3
  //   P2
  //   P1
  //   Display only works for unsigned, gives hex.
endmodule

module FA (
  input  IN_1,
  input  IN_2,
  input  C_IN,
  output S,
  output C_OUT
);

  wire and_1_out, and_2_out, xor_1_out;

  xor xor_1 (xor_1_out, IN_1, IN_2);
  xor xor_2 (S, xor_1_out, C_IN);
  and and_1 (and_1_out, IN_1, IN_2);
  and and_2 (and_2_out, xor_1_out, C_IN);
  or or_1 (C_OUT, and_1_out, and_2_out);
endmodule

module HA (
  input  IN_1,
  input  IN_2,
  output S,
  output C_OUT
);

  xor xor_1 (S, IN_1, IN_2);
  and and_1 (C_OUT, IN_1, IN_2);
endmodule
