// Logisim project oblig1.circ as structural Verilog: 1 circuit, main circuit main
module main (
  input  A3,
  input  A2,
  input  A1,
  input  A0,
  output [8:0] x___10,
  output [8:0] x___8,
  output [8:0] x,
  output [8:0] x____10
);

  wire adder_1_cout;
  wire [8:0] adder_1_out, not_1_out;

  Adder #(.width(9)) adder_1 (
    .a({2'b00, A3, A2, A1, A0, 3'b000}), .b({{5{1'b0}}, A3, A2, A1, A0}), .out(adder_1_out),
    .cout(adder_1_cout));  // open: cin
  Adder #(.width(9)) adder_2 (
    .a({{5{1'b0}}, A3, A2, A1, A0}), .b(adder_1_out), .out(x___10), .cin(adder_1_cout));  // open: cout
  assign not_1_out = ~x___10;  // NOT_Gate not_1, 9 bits wide
  Adder #(.width(9)) adder_3 (.a(not_1_out), .b(9'h1), .out(x____10));  // open: cin, cout

  assign x = {{5{1'b0}}, A3, A2, A1, A0};
  assign x___8 = {2'b00, A3, A2, A1, A0, 3'b000};
endmodule
